# Fritzing sketch Circuito (saved by Fritzing 0.9.4)
breadboards: 1

parts:
  LED1 = smd LED [color="Red (633nm)" package="1206 [SMD]"]
  U2 = ENCODER-QUADRATURE [package=encoder-16mm-quad]
  Mod1 = L298N DC motor driver
  M1 = DC Motor
  M2 = fc-51 [package=THT]
  NodeMCU_v1 = NodeMCU v3 LoLin [part_number=ESP8266]
  V1 = DC Power [voltage=5]

nets:
  GND: LED1.cathode, Mod1.GND, M2.pin2, NodeMCU_v1.GND, V1.V-
  N1: LED1.anode, NodeMCU_v1.D8
  N2: U2.B, NodeMCU_v1.D4
  N3: U2.C, NodeMCU_v1.D3
  N4: Mod1.12V, V1.V+
  N5: Mod1.OUT3, M1.pin_2
  N6: Mod1.OUT4, M1.pin_1
  N7: Mod1.IN3, NodeMCU_v1.D2
  N8: Mod1.ENB, NodeMCU_v1.D1
  N9: M2.pin1, NodeMCU_v1.D7
  N10: M2.pin3, NodeMCU_v1.3V3

custom parts:
  L298N DC motor driver: 2x DC motor driver with 78M05 positive voltage regulator (7..35 V) L298N: max 46 V, 2 A Set 5 V Enable jumper to enable 5 V regultor (needed for the L298N) and +5 V output at screw terminal or supply external +5 V at screw terminal Set ENA and/or ENB to +5 V to enable motor permanently or supply ENA and/or ENB with PWM signal IN1 and IN2 set rotation directory for motor A (OUT1/OUT2) IN2 and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
  NodeMCU v3 LoLin: NodeMCU v3 LoLin NodeMCU (http://www.nodemcu.com/) is an open source IoT platform. It includes firmware (https://nodemcu-build.com/) which runs on the ESP8266 Wi-Fi SoC from Espressif Systems, and hardware which is based on the ESP-12E module. The term "NodeMCU" by default refers to the firmware rather than the dev kits. The firmware uses the Lua scripting language. It is based on the eLua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
